# Fritzing sketch hw-rgb-power-led (saved by Fritzing 0.9.3b)
breadboards: 1

parts:
  Componente1 = Arduino Uno (Rev3)  # not connected
  R1 = Resistor [tolerance=±5% resistance=10 power=1W package=THT]
  Power_RGB1 = Prolight RGB 3 Watt Star
  R2 = Resistor [tolerance=±5% resistance=10 power=1W package=THT]  # not connected
  R3 = Resistor [tolerance=±5% resistance=10 power=1W package=THT]

nets:
  N1: R1.Pin_0, R3.Pin_0
  N2: R1.Pin_1, Power_RGB1.B+, R3.Pin_1
  N3: Power_RGB1.R-, Power_RGB1.G-, Power_RGB1.B-
