# Fritzing sketch hw-rgb-with-3-leds (saved by Fritzing 0.9.3b)
breadboards: 1

parts:
  Componente1 = Arduino Uno (Rev3)
  R1 = Resistor [tolerance=±5% resistance=220 package=THT]
  R2 = Resistor [tolerance=±5% resistance=220 package=THT]
  R3 = Resistor [tolerance=±5% resistance=220 package=THT]
  LED1 = LED - 5mm [color="Red (633nm)" package="5 mm [THT]"]
  LED2 = LED - 5mm [color="Green (560nm)" package="5 mm [THT]"]
  LED3 = LED - 5mm [color="Blue (470nm)" package="5 mm [THT]"]

nets:
  N1: Componente1.GND, LED1.cathode, LED2.cathode
  N2: Componente1.D3_PWM, R1.Pin_0, R3.Pin_1, LED3.anode
  N3: Componente1.D5_PWM, R2.Pin_0
  N4: Componente1.D6_PWM, R3.Pin_0
  N5: R1.Pin_1, LED1.anode
  N6: R2.Pin_1, LED2.anode
